// Digital circuit 1X15_RAM.dig as structural Verilog
module _1X15_RAM (
  input  RS1,
  input  RS2,
  input  WS,
  input  [14:0] WD_14_0,
  input  CLK,
  output [14:0] RD1_14_0,
  output [14:0] RD2_14_0
);

  _1x1_RAM _1x1_ram_1 (
    .WD(WD_14_0[14]), .WS(WS), .RS1(RS1), .RS2(RS2), .CLK(CLK), .RD1(RD1_14_0[14]), .RD2(RD2_14_0[14]));
  _1x1_RAM _1x1_ram_2 (
    .WD(WD_14_0[13]), .WS(WS), .RS1(RS1), .RS2(RS2), .CLK(CLK), .RD1(RD1_14_0[13]), .RD2(RD2_14_0[13]));
  _1x1_RAM _1x1_ram_3 (
    .WD(WD_14_0[12]), .WS(WS), .RS1(RS1), .RS2(RS2), .CLK(CLK), .RD1(RD1_14_0[12]), .RD2(RD2_14_0[12]));
  _1x1_RAM _1x1_ram_4 (
    .WD(WD_14_0[11]), .WS(WS), .RS1(RS1), .RS2(RS2), .CLK(CLK), .RD1(RD1_14_0[11]), .RD2(RD2_14_0[11]));
  _1x1_RAM _1x1_ram_5 (
    .WD(WD_14_0[10]), .WS(WS), .RS1(RS1), .RS2(RS2), .CLK(CLK), .RD1(RD1_14_0[10]), .RD2(RD2_14_0[10]));
  _1x1_RAM _1x1_ram_6 (.WD(WD_14_0[9]), .WS(WS), .RS1(RS1), .RS2(RS2), .CLK(CLK), .RD1(RD1_14_0[9]), .RD2(RD2_14_0[9]));
  _1x1_RAM _1x1_ram_7 (.WD(WD_14_0[8]), .WS(WS), .RS1(RS1), .RS2(RS2), .CLK(CLK), .RD1(RD1_14_0[8]), .RD2(RD2_14_0[8]));
  _1x1_RAM _1x1_ram_8 (.WD(WD_14_0[7]), .WS(WS), .RS1(RS1), .RS2(RS2), .CLK(CLK), .RD1(RD1_14_0[7]), .RD2(RD2_14_0[7]));
  _1x1_RAM _1x1_ram_9 (.WD(WD_14_0[6]), .WS(WS), .RS1(RS1), .RS2(RS2), .CLK(CLK), .RD1(RD1_14_0[6]), .RD2(RD2_14_0[6]));
  _1x1_RAM _1x1_ram_10 (
    .WD(WD_14_0[5]), .WS(WS), .RS1(RS1), .RS2(RS2), .CLK(CLK), .RD1(RD1_14_0[5]), .RD2(RD2_14_0[5]));
  _1x1_RAM _1x1_ram_11 (
    .WD(WD_14_0[4]), .WS(WS), .RS1(RS1), .RS2(RS2), .CLK(CLK), .RD1(RD1_14_0[4]), .RD2(RD2_14_0[4]));
  _1x1_RAM _1x1_ram_12 (
    .WD(WD_14_0[3]), .WS(WS), .RS1(RS1), .RS2(RS2), .CLK(CLK), .RD1(RD1_14_0[3]), .RD2(RD2_14_0[3]));
  _1x1_RAM _1x1_ram_13 (
    .WD(WD_14_0[2]), .WS(WS), .RS1(RS1), .RS2(RS2), .CLK(CLK), .RD1(RD1_14_0[2]), .RD2(RD2_14_0[2]));
  _1x1_RAM _1x1_ram_14 (
    .WD(WD_14_0[1]), .WS(WS), .RS1(RS1), .RS2(RS2), .CLK(CLK), .RD1(RD1_14_0[1]), .RD2(RD2_14_0[1]));
  _1x1_RAM _1x1_ram_15 (
    .WD(WD_14_0[0]), .WS(WS), .RS1(RS1), .RS2(RS2), .CLK(CLK), .RD1(RD1_14_0[0]), .RD2(RD2_14_0[0]));

  // Other names for the same wires on the sheet: RD10 = RD1_14_0[0]; RD11 = RD1_14_0[1]; RD12 = RD1_14_0[2];
  //   RD13 = RD1_14_0[3]; RD14 = RD1_14_0[4]; RD15 = RD1_14_0[5]; RD16 = RD1_14_0[6]; RD17 = RD1_14_0[7];
  //   RD18 = RD1_14_0[8]; RD19 = RD1_14_0[9]; RD20 = RD2_14_0[0]; RD21 = RD2_14_0[1]; RD22 = RD2_14_0[2];
  //   RD23 = RD2_14_0[3]; RD24 = RD2_14_0[4]; RD25 = RD2_14_0[5]; RD26 = RD2_14_0[6]; RD27 = RD2_14_0[7];
  //   RD28 = RD2_14_0[8]; RD29 = RD2_14_0[9]; RD110 = RD1_14_0[10]; RD111 = RD1_14_0[11]; RD112 = RD1_14_0[12];
  //   RD113 = RD1_14_0[13]; RD114 = RD1_14_0[14]; RD210 = RD2_14_0[10]; RD211 = RD2_14_0[11]; RD212 = RD2_14_0[12];
  //   RD213 = RD2_14_0[13]; RD214 = RD2_14_0[14]; wd0 = WD_14_0[0]; wd1 = WD_14_0[1]; wd2 = WD_14_0[2];
  //   wd3 = WD_14_0[3]; wd4 = WD_14_0[4]; wd5 = WD_14_0[5]; wd6 = WD_14_0[6]; wd7 = WD_14_0[7]; wd8 = WD_14_0[8];
  //   wd9 = WD_14_0[9]; wd10 = WD_14_0[10]; wd11 = WD_14_0[11]; wd12 = WD_14_0[12]; wd13 = WD_14_0[13];
  //   wd14 = WD_14_0[14]
endmodule
