// Digital circuit 1x1_RAM.dig as structural Verilog
module _1x1_RAM (
  input  WD,
  input  WS,
  input  CLK,
  input  RS1,
  input  RS2,
  output RD1,
  output RD2
);

  wire d_ff_1_q, multiplexer_1_out;

  Multiplexer multiplexer_1 (.sel(WS), .in_0(d_ff_1_q), .in_1(WD), .out(multiplexer_1_out));
  D_FF d_ff_1 (.D(multiplexer_1_out), .C(CLK), .Q(d_ff_1_q));  // open: nQ
  and and_1 (RD1, RS1, d_ff_1_q);
  and and_2 (RD2, RS2, d_ff_1_q);

  // Other names for the same wires on the sheet: rd1_t = RS1; rd2_t = RS2
endmodule
