// Digital circuit 3_Bit_ProgramCounter.dig as structural Verilog
module _3_Bit_ProgramCounter (
  input  [2:0] I_2_0,
  input  CLK,
  output [2:0] O_2_0
);

  wire [3:3] _4bitreg_1_dout_3_0;

  _4bitreg _4bitreg_1 (.Din_3_0({1'b0, I_2_0}), .Sel(1'b1), .CLK(CLK), .Dout_3_0({_4bitreg_1_dout_3_0[3], O_2_0}));
  // also tied to GND on the sheet: _4bitreg_1_dout_3_0[3]
endmodule
