// Digital circuit 4'bADDER.dig as structural Verilog
module _4_bADDER (
  input  [3:0] A_3_0,
  input  [3:0] B_3_0,
  output [3:0] S_3_0,
  output Cout
);

  wire fa_2_cout, fa_3_cout, fa_4_cout;

  FA fa_1 (.A(A_3_0[3]), .B(B_3_0[3]), .Cin(fa_2_cout), .S(S_3_0[3]), .Cout(Cout));
  FA fa_2 (.A(A_3_0[2]), .B(B_3_0[2]), .Cin(fa_3_cout), .S(S_3_0[2]), .Cout(fa_2_cout));
  FA fa_3 (.A(A_3_0[1]), .B(B_3_0[1]), .Cin(fa_4_cout), .S(S_3_0[1]), .Cout(fa_3_cout));
  FA fa_4 (.A(A_3_0[0]), .B(B_3_0[0]), .Cin(1'b0), .S(S_3_0[0]), .Cout(fa_4_cout));

  // Other names for the same wires on the sheet: a0 = A_3_0[0]; a1 = A_3_0[1]; a2 = A_3_0[2]; a3 = A_3_0[3];
  //   b0 = B_3_0[0]; b1 = B_3_0[1]; b2 = B_3_0[2]; b3 = B_3_0[3]; s0 = S_3_0[0]; s1 = S_3_0[1]; s2 = S_3_0[2];
  //   s3 = S_3_0[3]
endmodule
