// Digital circuit 4'bNot.dig as structural Verilog
module _4_bNot (
  input  [3:0] A_3_0,
  output [3:0] O_3_0
);

  not not_1 (O_3_0[0], A_3_0[0]);
  not not_2 (O_3_0[1], A_3_0[1]);
  not not_3 (O_3_0[2], A_3_0[2]);
  not not_4 (O_3_0[3], A_3_0[3]);
endmodule
