// Digital circuit 4bitALU.dig as structural Verilog
module _4bitALU (
  input  [3:0] A,
  input  [3:0] B,
  input  [1:0] OP,
  output [3:0] R
);

  wire [3:0] _4_badder_1_s_3_0, _4_bnot_1_o_3_0, _4bitrol_1_o_3_0;

  _4_bNot _4_bnot_1 (.A_3_0(A), .O_3_0(_4_bnot_1_o_3_0));
  _4_bADDER _4_badder_1 (.A_3_0(A), .B_3_0(B), .S_3_0(_4_badder_1_s_3_0));  // open: Cout
  _4bitROL _4bitrol_1 (.A_3_0(A), .B_3_0(B), .O_3_0(_4bitrol_1_o_3_0));
  Multiplexer #(.Selector_Bits(2), .Bits(4)) multiplexer_1 (
    .sel(OP), .in_0(_4_bnot_1_o_3_0), .in_1(_4_badder_1_s_3_0), .in_2(_4bitrol_1_o_3_0), .in_3(4'b0000),
    .out(R));
endmodule
