// Digital circuit 4bitROL.dig as structural Verilog
module _4bitROL (
  input  [3:0] B_3_0,
  input  [3:0] A_3_0,
  output [3:0] O_3_0
);

  Multiplexer #(.Selector_Bits(4)) multiplexer_1 (
    .sel(B_3_0), .in_0(A_3_0[3]), .in_1(A_3_0[2]), .in_2(A_3_0[1]), .in_3(A_3_0[0]), .in_4(1'b0),
    .in_5(1'b0), .in_6(1'b0), .in_7(1'b0), .in_8(1'b0), .in_9(1'b0), .in_10(1'b0), .in_11(1'b0),
    .in_12(1'b0), .in_13(1'b0), .in_14(1'b0), .in_15(1'b0), .out(O_3_0[3]));
  Multiplexer #(.Selector_Bits(4)) multiplexer_2 (
    .sel(B_3_0), .in_0(A_3_0[2]), .in_1(A_3_0[1]), .in_2(A_3_0[0]), .in_3(A_3_0[3]), .in_4(1'b0),
    .in_5(1'b0), .in_6(1'b0), .in_7(1'b0), .in_8(1'b0), .in_9(1'b0), .in_10(1'b0), .in_11(1'b0),
    .in_12(1'b0), .in_13(1'b0), .in_14(1'b0), .in_15(1'b0), .out(O_3_0[2]));
  Multiplexer #(.Selector_Bits(4)) multiplexer_3 (
    .sel(B_3_0), .in_0(A_3_0[1]), .in_1(A_3_0[0]), .in_2(A_3_0[3]), .in_3(A_3_0[2]), .in_4(1'b0),
    .in_5(1'b0), .in_6(1'b0), .in_7(1'b0), .in_8(1'b0), .in_9(1'b0), .in_10(1'b0), .in_11(1'b0),
    .in_12(1'b0), .in_13(1'b0), .in_14(1'b0), .in_15(1'b0), .out(O_3_0[1]));
  Multiplexer #(.Selector_Bits(4)) multiplexer_4 (
    .sel(B_3_0), .in_0(A_3_0[0]), .in_1(A_3_0[3]), .in_2(A_3_0[2]), .in_3(A_3_0[1]), .in_4(1'b0),
    .in_5(1'b0), .in_6(1'b0), .in_7(1'b0), .in_8(1'b0), .in_9(1'b0), .in_10(1'b0), .in_11(1'b0),
    .in_12(1'b0), .in_13(1'b0), .in_14(1'b0), .in_15(1'b0), .out(O_3_0[0]));

  // Other names for the same wires on the sheet: a0 = A_3_0[0]; a1 = A_3_0[1]; a2 = A_3_0[2]; a3 = A_3_0[3];
  //   O0 = O_3_0[0]; O1 = O_3_0[1]; O2 = O_3_0[2]; O3 = O_3_0[3]

  // Notes on the sheet:
  //   1 bit 16 to 1 MUX
endmodule
