// Digital circuit 4bit_CU.dig as structural Verilog
module _4bit_CU (
  input  [3:0] Opcode_3_0,
  input  ZF,
  output [1:0] OP_1_0,
  output WE,
  output Imm_sel,
  output JMP_sel
);

  wire and_1_out, and_3_out, and_4_out, and_5_out, or_2_out;

  and and_1 (and_1_out, ~Opcode_3_0[2], ~Opcode_3_0[3]);  // And
  and and_2 (Imm_sel, ~Opcode_3_0[3], Opcode_3_0[2]);  // And
  and and_3 (and_3_out, Opcode_3_0[3], ~Opcode_3_0[2]);  // And
  and and_4 (and_4_out, ~Opcode_3_0[0], ~Opcode_3_0[1]);  // And
  and and_5 (and_5_out, Opcode_3_0[0], ~Opcode_3_0[1], ~ZF);  // And
  or or_1 (WE, and_1_out, Imm_sel);
  or or_2 (or_2_out, and_4_out, and_5_out);
  and and_6 (JMP_sel, and_3_out, or_2_out);

  assign OP_1_0 = Opcode_3_0[1:0];
endmodule
