// Digital circuit 4bitreg.dig as structural Verilog
module _4bitreg (
  input  [3:0] Din_3_0,
  input  Sel,
  input  CLK,
  output [3:0] Dout_3_0
);

  _1bitreg _1bitreg_1 (.Din(Din_3_0[0]), .Sel(Sel), .CLK(CLK), .Dout(Dout_3_0[0]));
  _1bitreg _1bitreg_2 (.Din(Din_3_0[1]), .Sel(Sel), .CLK(CLK), .Dout(Dout_3_0[1]));
  _1bitreg _1bitreg_3 (.Din(Din_3_0[2]), .Sel(Sel), .CLK(CLK), .Dout(Dout_3_0[2]));
  _1bitreg _1bitreg_4 (.Din(Din_3_0[3]), .Sel(Sel), .CLK(CLK), .Dout(Dout_3_0[3]));

  // Notes on the sheet:
  //   4 Bit Register
endmodule
