// Digital circuit 8x15_RAM.dig as structural Verilog
module _8x15_RAM (
  input  [2:0] RA1_2_0,
  input  [2:0] RA2_2_0,
  input  [2:0] WR_2_0,
  input  [14:0] WRD_14_0,
  input  WE,
  input  CLK,
  output [14:0] RD1_14_0,
  output [14:0] RD2_14_0
);

  wire decoder_3_out_0, decoder_3_out_1, decoder_3_out_2, decoder_3_out_3, decoder_3_out_4, decoder_3_out_5,
       decoder_3_out_6, decoder_3_out_7, R1_0, R1_1, R1_2, R1_3, R1_4, R1_5, R1_6, R1_7, R2_0, R2_1, R2_2,
       R2_3, R2_4, R2_5, R2_6, R2_7, WA_0, WA_1, WA_2, WA_3, WA_4, WA_5, WA_6, WA_7;
  wire [14:0] RD1_0, RD1_1, RD1_2, RD1_3, RD1_4, RD1_5, RD1_6, RD1_7, RD2_0, RD2_1, RD2_2, RD2_3, RD2_4,
       RD2_5, RD2_6, RD2_7;

  Decoder #(.Selector_Bits(3)) decoder_1 (
    .sel(RA1_2_0), .out_0(R1_0), .out_1(R1_1), .out_2(R1_2), .out_3(R1_3), .out_4(R1_4), .out_5(R1_5),
    .out_6(R1_6), .out_7(R1_7));
  Decoder #(.Selector_Bits(3)) decoder_2 (
    .sel(RA2_2_0), .out_0(R2_0), .out_1(R2_1), .out_2(R2_2), .out_3(R2_3), .out_4(R2_4), .out_5(R2_5),
    .out_6(R2_6), .out_7(R2_7));
  Decoder #(.Selector_Bits(3)) decoder_3 (
    .sel(WR_2_0), .out_0(decoder_3_out_0), .out_1(decoder_3_out_1), .out_2(decoder_3_out_2),
    .out_3(decoder_3_out_3), .out_4(decoder_3_out_4), .out_5(decoder_3_out_5), .out_6(decoder_3_out_6),
    .out_7(decoder_3_out_7));
  AND_GATES_RAM and_gates_ram_1 (
    .EN(WE), .I_0(decoder_3_out_0), .I_1(decoder_3_out_1), .I_2(decoder_3_out_2), .I_3(decoder_3_out_3),
    .I_4(decoder_3_out_4), .I_5(decoder_3_out_5), .I_6(decoder_3_out_6), .I_7(decoder_3_out_7), .O_0(WA_0),
    .O_1(WA_1), .O_2(WA_2), .O_3(WA_3), .O_4(WA_4), .O_5(WA_5), .O_6(WA_6), .O_7(WA_7));
  _1X15_RAM RAM_0 (
    .RS1(R1_0), .RS2(R2_0), .WS(WA_0), .WD_14_0(WRD_14_0), .CLK(CLK), .RD1_14_0(RD1_0), .RD2_14_0(RD2_0));
  _1X15_RAM RAM_1 (
    .RS1(R1_1), .RS2(R2_1), .WS(WA_1), .WD_14_0(WRD_14_0), .CLK(CLK), .RD1_14_0(RD1_1), .RD2_14_0(RD2_1));
  _1X15_RAM RAM_2 (
    .RS1(R1_2), .RS2(R2_2), .WS(WA_2), .WD_14_0(WRD_14_0), .CLK(CLK), .RD1_14_0(RD1_2), .RD2_14_0(RD2_2));
  _1X15_RAM RAM_3 (
    .RS1(R1_3), .RS2(R2_3), .WS(WA_3), .WD_14_0(WRD_14_0), .CLK(CLK), .RD1_14_0(RD1_3), .RD2_14_0(RD2_3));
  _1X15_RAM RAM_4 (
    .RS1(R1_4), .RS2(R2_4), .WS(WA_4), .WD_14_0(WRD_14_0), .CLK(CLK), .RD1_14_0(RD1_4), .RD2_14_0(RD2_4));
  _1X15_RAM RAM_5 (
    .RS1(R1_5), .RS2(R2_5), .WS(WA_5), .WD_14_0(WRD_14_0), .CLK(CLK), .RD1_14_0(RD1_5), .RD2_14_0(RD2_5));
  _1X15_RAM RAM_6 (
    .RS1(R1_6), .RS2(R2_6), .WS(WA_6), .WD_14_0(WRD_14_0), .CLK(CLK), .RD1_14_0(RD1_6), .RD2_14_0(RD2_6));
  _1X15_RAM RAM_7 (
    .RS1(R1_7), .RS2(R2_7), .WS(WA_7), .WD_14_0(WRD_14_0), .CLK(CLK), .RD1_14_0(RD1_7), .RD2_14_0(RD2_7));
  assign RD1_14_0 = RD1_0 | RD1_1 | RD1_2 | RD1_3 | RD1_4 | RD1_5 | RD1_6 | RD1_7;  // Or or_1, 15 bits wide
  assign RD2_14_0 = RD2_0 | RD2_1 | RD2_2 | RD2_3 | RD2_4 | RD2_5 | RD2_6 | RD2_7;  // Or or_2, 15 bits wide

  // Other names for the same wires on the sheet: WD[14:0] = WRD_14_0
endmodule
