// Digital circuit AND_GATES_RAM.dig as structural Verilog
module AND_GATES_RAM (
  input  EN,
  input  I_0,
  input  I_1,
  input  I_2,
  input  I_3,
  input  I_4,
  input  I_5,
  input  I_6,
  input  I_7,
  output O_0,
  output O_1,
  output O_2,
  output O_3,
  output O_4,
  output O_5,
  output O_6,
  output O_7
);

  and and_1 (O_0, EN, I_0);
  and and_2 (O_1, EN, I_1);
  and and_3 (O_2, EN, I_2);
  and and_4 (O_3, EN, I_3);
  and and_5 (O_4, EN, I_4);
  and and_6 (O_5, EN, I_5);
  and and_7 (O_6, EN, I_6);
  and and_8 (O_7, EN, I_7);
endmodule
