// Digital circuit CPU.dig as structural Verilog
module CPU (
  input  [2:0] WR_2_0,
  input  [14:0] WRD_14_0,
  input  WE,
  input  CLK,
  input  PC_EN,
  input  [2:0] RA2_2_0,
  input  ZF,
  output [3:0] R_3_0,
  output [14:0] RD2,
  output [3:0] A_3_0,
  output [1:0] Reg1_1_0,
  output [1:0] Reg2_1_0,
  output [1:0] OP_1_0,
  output [3:0] B_3_0,
  output [1:0] Wr_1_0,
  output [2:0] JMP_ADDR_2_0
);

  wire _4bit_cu_1_we, CPU_CLK, Imm_sel, JMP_SEL;
  wire [2:0] _3_bit_programcounter_1_o_2_0, _3bit_pc_adder_1_o_2_0, multiplexer_1_out;
  wire [3:0] registerset4_1_b_3_0;
  wire [6:0] Don_t_Care;
  wire [14:11] _8x15_ram_1_rd1_14_0;

  Multiplexer #(.Bits(3)) multiplexer_1 (
    .sel(JMP_SEL), .in_0(_3bit_pc_adder_1_o_2_0), .in_1(JMP_ADDR_2_0), .out(multiplexer_1_out));
  _3bit_PC_Adder _3bit_pc_adder_1 (.I_2_0(_3_bit_programcounter_1_o_2_0), .O_2_0(_3bit_pc_adder_1_o_2_0));
  _3_Bit_ProgramCounter _3_bit_programcounter_1 (
    .I_2_0(multiplexer_1_out), .CLK(CPU_CLK), .O_2_0(_3_bit_programcounter_1_o_2_0));
  and and_1 (CPU_CLK, PC_EN, CLK);
  _8x15_RAM _8x15_ram_1 (
    .RA1_2_0(_3_bit_programcounter_1_o_2_0), .RA2_2_0(RA2_2_0), .WR_2_0(WR_2_0), .WRD_14_0(WRD_14_0),
    .WE(WE), .CLK(CLK), .RD1_14_0({_8x15_ram_1_rd1_14_0, JMP_ADDR_2_0, Reg2_1_0[0], Don_t_Care}),
    .RD2_14_0(RD2));
  _4bit_CU _4bit_cu_1 (
    .Opcode_3_0(_8x15_ram_1_rd1_14_0), .ZF(ZF), .OP_1_0(OP_1_0), .WE(_4bit_cu_1_we), .Imm_sel(Imm_sel),
    .JMP_sel(JMP_SEL));
  RegisterSet4 registerset4_1 (
    .Wr_1_0(JMP_ADDR_2_0[2:1]), .CLK(CPU_CLK), .WE(_4bit_cu_1_we), .Wrd_3_0(R_3_0),
    .Ra_1_0(JMP_ADDR_2_0[2:1]), .Rb_1_0({JMP_ADDR_2_0[0], Reg2_1_0[0]}), .A_3_0(A_3_0),
    .B_3_0(registerset4_1_b_3_0));
  _4bitALU _4bitalu_1 (.A(A_3_0), .B(B_3_0), .OP(OP_1_0), .R(R_3_0));
  Multiplexer #(.Bits(4)) multiplexer_2 (
    .sel(Imm_sel), .in_0(registerset4_1_b_3_0), .in_1({JMP_ADDR_2_0[0], Reg2_1_0[0], Don_t_Care[6:5]}),
    .out(B_3_0));

  assign Reg1_1_0 = JMP_ADDR_2_0[2:1];
  assign Reg2_1_0[1] = JMP_ADDR_2_0[0];
  assign Wr_1_0 = JMP_ADDR_2_0[2:1];

  // Other names for the same wires on the sheet: Im_val[3:0] = {JMP_ADDR_2_0[0], Reg2_1_0[0], Don_t_Care[6:5]};
  //   Reg2[1:0] = {JMP_ADDR_2_0[0], Reg2_1_0[0]}; JMP_ADDR[2:0] = JMP_ADDR_2_0; Reg1[1:0] = JMP_ADDR_2_0[2:1];
  //   A[3:0] = A_3_0; B[3:0] = B_3_0; OP[1:0] = OP_1_0; R[3:0] = R_3_0; WD[14:0] = WRD_14_0

  // Notes on the sheet:
  //   Register Mode(Type of OP 00) : 2 bit(type of OP)+2bit(OP)+2bit(Reg1)+2bit(Reg2) + 7bit (Don't Care)
  //   Immidiate Mode(Type of OP 01) :  2 bit(type of OP)+2bit(OP)+2bit(Reg1)+4bit(Imm value) + 5bit (Don't Care)
  //   Jump Mode(Type of OP 10) :  2 bit(type of OP)+2bit(OP)+3bit(Jump Address)+8 bit (Don't Care)
  //   OP(00): NOT , OP(01):ADD , OP(11):ROL
  //   OP(00): JMP , OP(01):JNE
  //   JNE START
  //   100100100000000
  //   ADD R1,0101
  //   010101010100000
  //   JMP ADD1
  //   100000100000000
endmodule
