// Digital circuit RegisterSet4.dig as structural Verilog
module RegisterSet4 (
  input  [1:0] Wr_1_0,
  input  WE,
  input  CLK,
  input  [3:0] Wrd_3_0,
  input  [1:0] Ra_1_0,
  input  [1:0] Rb_1_0,
  output [3:0] A_3_0,
  output [3:0] B_3_0
);

  wire and_1_out, and_2_out, and_3_out, and_4_out, r0, r1, r2, r3;
  wire [3:0] R0_dout_3_0, R1_dout_3_0, R2_dout_3_0, R3_dout_3_0;

  Decoder #(.Selector_Bits(2)) decoder_1 (.sel(Wr_1_0), .out_0(r0), .out_1(r1), .out_2(r2), .out_3(r3));
  and and_1 (and_1_out, r0, WE);
  and and_2 (and_2_out, r1, WE);
  and and_3 (and_3_out, r2, WE);
  and and_4 (and_4_out, r3, WE);
  _4bitreg u_R0 (.Din_3_0(Wrd_3_0), .Sel(and_1_out), .CLK(CLK), .Dout_3_0(R0_dout_3_0));
  _4bitreg u_R1 (.Din_3_0(Wrd_3_0), .Sel(and_2_out), .CLK(CLK), .Dout_3_0(R1_dout_3_0));
  _4bitreg u_R2 (.Din_3_0(Wrd_3_0), .Sel(and_3_out), .CLK(CLK), .Dout_3_0(R2_dout_3_0));
  _4bitreg u_R3 (.Din_3_0(Wrd_3_0), .Sel(and_4_out), .CLK(CLK), .Dout_3_0(R3_dout_3_0));
  Multiplexer #(.Selector_Bits(2), .Bits(4)) multiplexer_1 (
    .sel(Ra_1_0), .in_0(R0_dout_3_0), .in_1(R1_dout_3_0), .in_2(R2_dout_3_0), .in_3(R3_dout_3_0), .out(A_3_0));
  Multiplexer #(.Selector_Bits(2), .Bits(4)) multiplexer_2 (
    .sel(Rb_1_0), .in_0(R0_dout_3_0), .in_1(R1_dout_3_0), .in_2(R2_dout_3_0), .in_3(R3_dout_3_0), .out(B_3_0));

  // Other names for the same wires on the sheet: din[3:0] = Wrd_3_0; ra[1:0] = Ra_1_0; rb[1:0] = Rb_1_0; regen = WE
endmodule
